# Fritzing sketch schematic (saved by Fritzing 1.0.1rc)
breadboards: 1

parts:
  U1 = ESP32S-HiLetgo [part_number=ESP32S-HiLetgo]
  A1 = Waveshare SN65HVD230
  U3 = Sharp PC817 [package=THT]
  U4 = Mini-360 DC-DC Buck converter [package=THT]
  R1 = Resistor [tolerance=±5% power=0.25 resistance=220 package=THT]
  R2 = Resistor [tolerance=±5% power=0.25 resistance=1k package=THT]
  J2 = female pin header, 2 pins [form="♀ (female)"]
  J3 = male pin header, 2 pins [form="♂ (male)"]
  J1 = screw terminal, 8 pins
  S1 = Illuminated Pushbutton
  RY1 = KF-301 Relay [package=THT]

nets:
  3.3V: U1.3.3, A1.Pin_1
  GND: U1.GND, A1.Pin_2, U3.Pin_2, U4.IN-, U4.OUT-, J1.pin8, S1.S-1, S1.LED-, RY1.ground
  5V: U1.VIN, U4.OUT+, RY1.power
  N1: U1.GPIO4, A1.Pin_3
  N2: U1.GPIO16, A1.Pin_4
  N3: U1.GPIO17, R2.Pin_0
  N4: U1.GPIO5, J2.pin1
  N5: U1.GPIO18, R1.Pin_0
  N6: U1.GPIO19, RY1.signal
  N7: A1.Pin_5, A1.Pin_7, J1.pin6
  N8: A1.Pin_6, A1.Pin_8, J1.pin7
  N9: U3.Pin_1, R1.Pin_1
  12V: U3.Pin_4, U4.IN+, J1.pin1
  N10: U3.Pin_3, J1.pin2
  N11: R2.Pin_1, J2.pin2
  N12: J3.pin1, S1.S-2
  N13: J3.pin2, S1.LED+
  N14: J1.pin3, RY1.NC
  N15: J1.pin4, RY1.C
  N16: J1.pin5, RY1.NO

notes:
  acc
  trigger
  back_cam_in
  front_cam_in
  cam_out
  can_h
  can_l
  gnd

custom parts:
  ESP32S-HiLetgo: HiLetgo ESP-WROOM-32 ESP32 ESP-32S Development Board 2.4GHz Dual-Mode WiFi + Bluetooth Dual Cores Microcontroller The ESP32 integrated with Antenna switches, RF Balun, power amplifiers, low-noise amplifiers, filters, and management modules, and the entire solution occupies the least area of PCB. 2.4 GHz Wi-Fi plus Bluetooth dual-mode chip, with TSMC Ultra-low power consumption 40nm technology,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
  Waveshare SN65HVD230: The SN65HVD230 CAN Board is an accessory board features an onboard CAN transceiver SN65HVD230, which is pinout compatible with PCA82C250. It is powered from 3.3V and features ESD protection.
  Mini-360 DC-DC Buck converter: Mini-360 DC-DC Buck converter. Tiny buck step down voltage converter, input voltage 4.75 to 23V output 1 to 17V adjustable. Available from ebay and the like.
  KF-301 Relay: KF-301 SPDT Relay module using SRD-05VDC-SL-C relay.
